# Fritzing sketch Layout (saved by Fritzing 0.9.4)
circuit board: 8.46667cm x 5.64444cm
breadboards: 1

parts:
  WeMos_D1_Mini_WS2812B_RGB_Shield1 = WeMos D1 Mini WS2812B RGB Shield
  3V_Relay = RELAY [package=relay-g5q]
  I/O_Pwr = Square Pushbutton
  5V_Sby = LIPO-110mAh [package=lipo-110]
  I/O_5V_Pwr = Square Pushbutton

nets:
  N1: WeMos_D1_Mini_WS2812B_RGB_Shield1.5V, 5V_Sby.+, I/O_5V_Pwr.leg1
  N2: WeMos_D1_Mini_WS2812B_RGB_Shield1.D6, 3V_Relay.COIL1
  N3: WeMos_D1_Mini_WS2812B_RGB_Shield1.D7, I/O_5V_Pwr.leg0
  N4: WeMos_D1_Mini_WS2812B_RGB_Shield1.G, 3V_Relay.COIL2, 5V_Sby.-
  N5: 3V_Relay.MAIN, I/O_Pwr.leg1
  N6: 3V_Relay.NO, I/O_Pwr.leg0
